# Fritzing sketch legotest2 (saved by Fritzing 0.8.5b)
breadboards: 1

parts:
  Part1 = Arduino Uno (Rev3)
  IR1 = TSOP312.., 314.. [package=THT]
  LED1 = LED - 5mm [color="Infrared (850nm)" package="5 mm [THT]"]
  Part2 = ACS712 Low Current Sensor Board v12
  J1 = Basic Servo
  M1 = DC Motor
  M2 = DC Motor
  R1 = Resistor [tolerance=±5% resistance=220 package=THT]
  R2 = Resistor [tolerance=±5% resistance=1k package=THT]
  S1 = Toggle Switch [package=THT]
  R3 = Resistor [tolerance=±5% resistance=1k package=THT]
  D1 = Rectifier Diode [part_number=1N4001 package="300 mil [THT]"]
  D2 = Rectifier Diode [part_number=1N4001 package="300 mil [THT]"]
  D3 = Rectifier Diode [part_number=1N4001 package="300 mil [THT]"]
  D4 = Rectifier Diode [part_number=1N4001 package="300 mil [THT]"]
  Part4 = Arduino Motor Shield (Rev3)
  Part5 = ACS712 Low Current Sensor Board v12
  D5 = Rectifier Diode [part_number=1N4001 package="300 mil [THT]"]
  D6 = Rectifier Diode [part_number=1N4001 package="300 mil [THT]"]
  D7 = Rectifier Diode [part_number=1N4001 package="300 mil [THT]"]
  D8 = Rectifier Diode [part_number=1N4001 package="300 mil [THT]"]
  JACK1 = 2.1mm Barrel Jack with Terminal Block

nets:
  N1: Part1.A0, Part5.VO
  N2: Part1.A1, Part2.VO
  N3: Part1.D10_PWM/SS, R2.Pin_1
  N4: Part1.D13/SCK, R1.Pin_0
  GND: Part1.GND, IR1.Vs, LED1.cathode, Part2.GND, S1.L1, Part5.GND
  N5: Part1.D2, S1.COM, R3.Pin_0
  5V: Part1.5V, IR1.Data, Part2.5V, R3.Pin_1, Part5.5V
  N6: IR1.GND, R1.Pin_1
  N7: LED1.anode, R2.Pin_0
  N8: Part2.IP+, D1.cathode, D2.cathode
  N9: Part2.IP-, D3.anode, D4.anode
  GND_2: J1.gnd, Part4.GND, JACK1.NEG
  VCC: J1.vcc, Part4.5V
  N10: J1.pulse, Part4.A3
  N11: M1.pin_1, Part4.B+
  N12: M1.pin_2, D5.cathode, D8.anode
  N13: M2.pin_1, Part4.A+
  N14: M2.pin_2, D1.anode, D4.cathode
  N15: D2.anode, D3.cathode, Part4.A-
  N16: Part4.B-, D6.cathode, D7.anode
  N17: Part4.VMOT, JACK1.POS
  N18: Part5.IP+, D7.cathode, D8.cathode
  N19: Part5.IP-, D5.anode, D6.anode

notes:
  9v power supply for the motor shield
  9v power supply for the Arduino
  Push down motor
  Lift-arm motor
  Lift-arm modes selection servo
  Brick detection IR sensor
  ON/OFF switch
